# Fritzing sketch Finaler Aufbau Fritzing (saved by Fritzing 0.9.4)
breadboards: 2

parts:
  Bauteil1 = Arduino Nano (Rev3.0)
  Bauteil2 = Arduino Nano (Rev3.0)
  LCD1 = LCD screen
  LCM1602_IIC1 = LCM1602 IIC [part_number="LCM1602 IIC" chip_label="LCM1602 IIC" package="DIP (Dual Inline) [THT]"]
  S1 = Pushbutton [package="[THT]"]
  S2 = Pushbutton [package="[THT]"]
  R1 = Resistor [tolerance=±1% resistance=100k package=THT]
  passive_Piezo_Speaker = Piezo Speaker
  R2 = Resistor [tolerance=±1% resistance=100k package=THT]

nets:
  GND: Bauteil1.GND, Bauteil2.GND, LCD1.VSS, LCM1602_IIC1.VSS, LCM1602_IIC1.GND, R1.Pin_1, R2.Pin_1
  N1: Bauteil1.D2, S2.Pin_1, S2.Pin_2, R1.Pin_0
  N2: Bauteil1.D3, S1.Pin_1, S1.Pin_2, R2.Pin_0
  N3: Bauteil1.D4, passive_Piezo_Speaker.pin2
  5V: Bauteil1.5V, Bauteil2.5V, LCM1602_IIC1.VCC, S1.Pin_3, S1.Pin_4, S2.Pin_3, S2.Pin_4
  N4: Bauteil1.A5, Bauteil2.A5, LCM1602_IIC1.SCL
  N5: Bauteil1.A4, Bauteil2.A4, LCM1602_IIC1.SDA
  VDD: LCD1.VDD, LCM1602_IIC1.VDD
  N6: LCD1.V0, LCM1602_IIC1.V0
  N7: LCD1.RS, LCM1602_IIC1.RS
  N8: LCD1.R/W, LCM1602_IIC1.RW
  N9: LCD1.E, LCM1602_IIC1.E
  N10: LCD1.DB0, LCM1602_IIC1.D0
  N11: LCD1.DB1, LCM1602_IIC1.D1
  N12: LCD1.DB2, LCM1602_IIC1.D2
  N13: LCD1.DB3, LCM1602_IIC1.D3
  N14: LCD1.DB4, LCM1602_IIC1.D4
  N15: LCD1.DB5, LCM1602_IIC1.D5
  N16: LCD1.DB6, LCM1602_IIC1.D6
  N17: LCD1.DB7, LCM1602_IIC1.D7
  N18: LCD1.LED+, LCM1602_IIC1.A
  N19: LCD1.LED-, LCM1602_IIC1.K

custom parts:
  LCM1602 IIC: I2C-Module to use a 1602 or 2004 LCD on with the wire.h libory Serial LCD Modul
