# Fritzing sketch Vorgabe (saved by Fritzing 0.9.3b)
breadboards: 2

parts:
  Bauteil1 = Arduino Nano (Rev3.0)
  Bauteil2 = Arduino Nano (Rev3.0)

nets:
  GND: Bauteil1.GND, Bauteil2.GND
  5V: Bauteil1.5V, Bauteil2.5V
  N1: Bauteil1.A5, Bauteil2.A5
  N2: Bauteil1.A4, Bauteil2.A4
